// Logisim project AdderSubCircuit.circ as structural Verilog: 1 circuit, main circuit AdderSub
module AdderSub (
  input  Sub,
  input  B3,
  input  B2,
  input  B1,
  input  B0,
  input  A3,
  input  A2,
  input  A1,
  input  A0
);

  wire n7486_1_pin3, n7486_1_pin6, n7486_1_pin7, n7486_1_pin8, n7486_1_pin11, n7486_1_pin14, n74283_1_pin1,
       n74283_1_pin4, n74283_1_pin10, n74283_1_pin13;

  _7486 #(.ShowInternalStructure("true"), .VccGndPorts("true")) u_7486_1 (
    .pin1(B3), .pin2(Sub), .pin3(n7486_1_pin3), .pin4(B2), .pin5(Sub), .pin6(n7486_1_pin6),
    .pin7(n7486_1_pin7), .pin14(n7486_1_pin14), .pin13(B1), .pin12(Sub), .pin11(n7486_1_pin11), .pin10(B0),
    .pin9(Sub), .pin8(n7486_1_pin8));
  _74283 #(.ShowInternalStructure("true"), .VccGndPorts("true")) u_74283_1 (
    .pin1(n74283_1_pin1), .pin2(n7486_1_pin11), .pin3(A1), .pin4(n74283_1_pin4), .pin5(A0),
    .pin6(n7486_1_pin8), .pin7(Sub), .pin8(n7486_1_pin7), .pin16(n7486_1_pin14), .pin15(n7486_1_pin6),
    .pin14(A2), .pin13(n74283_1_pin13), .pin12(A3), .pin11(n7486_1_pin3), .pin10(n74283_1_pin10));  // open: pin9
  LED O3 (.in(n74283_1_pin10));
  LED O2 (.in(n74283_1_pin13));
  LED O1 (.in(n74283_1_pin1));
  LED O0 (.in(n74283_1_pin4));
  // also tied to GND on the sheet: n7486_1_pin7
  // also tied to VCC on the sheet: n7486_1_pin14

  // Notes on the sheet:
  //   bulasl
  //   B3
  //   B2
  //   B1
  //   B0
endmodule
