// Logisim project LabFinal (1).circ as structural Verilog: 2 circuits, main circuit main
module main (
  input  A0,
  input  A1,
  input  A2,
  input  A3,
  input  B0,
  input  B1,
  input  B2,
  input  B3,
  input  S0,
  input  S1,
  input  AS
);

  wire n7408_1_pin8, n7408_1_pin11, n7486_1_pin3, n7486_1_pin6, n7486_1_pin7, n7486_1_pin8, n7486_1_pin11,
       n7486_1_pin14, n7486_2_pin3, n7486_2_pin6, n7486_2_pin8, n7486_2_pin11, n74153_1_pin4, n74153_1_pin5,
       n74153_1_pin7, n74153_1_pin9, n74153_1_pin11, n74153_1_pin12, n74153_2_pin4, n74153_2_pin7,
       n74153_2_pin9, n74153_2_pin12, n74283_1_pin1, n74283_1_pin4, n74283_1_pin10, n74283_1_pin13;

  _7486 #(.ShowInternalStructure("true"), .VccGndPorts("true")) u_7486_1 (
    .pin1(B3), .pin2(AS), .pin3(n7486_1_pin3), .pin4(B2), .pin5(AS), .pin6(n7486_1_pin6),
    .pin7(n7486_1_pin7), .pin14(n7486_1_pin14), .pin13(B1), .pin12(AS), .pin11(n7486_1_pin11), .pin10(B0),
    .pin9(AS), .pin8(n7486_1_pin8));
  _74283 #(.ShowInternalStructure("true"), .VccGndPorts("true")) u_74283_1 (
    .pin1(n74283_1_pin1), .pin2(n7486_1_pin11), .pin3(A1), .pin4(n74283_1_pin4), .pin5(A0),
    .pin6(n7486_1_pin8), .pin7(AS), .pin8(n7486_1_pin7), .pin16(n7486_1_pin14), .pin15(n7486_1_pin6),
    .pin14(A2), .pin13(n74283_1_pin13), .pin12(A3), .pin11(n7486_1_pin3), .pin10(n74283_1_pin10));  // open: pin9
  _7486 #(.ShowInternalStructure("true"), .VccGndPorts("true")) u_7486_2 (
    .pin1(A0), .pin2(B0), .pin3(n7486_2_pin3), .pin4(A1), .pin5(B1), .pin6(n7486_2_pin6),
    .pin7(n7486_1_pin7), .pin14(n7486_1_pin14), .pin13(A3), .pin12(B3), .pin11(n7486_2_pin11), .pin10(A2),
    .pin9(B2), .pin8(n7486_2_pin8));
  _74153 #(.ShowInternalStructure("true"), .VccGndPorts("true")) u_74153_1 (
    .pin1(n7486_1_pin7), .pin2(S1), .pin3(n7486_2_pin3), .pin4(n74153_1_pin4), .pin5(n74153_1_pin5),
    .pin6(n74283_1_pin4), .pin7(n74153_1_pin7), .pin8(n7486_1_pin7), .pin16(n7486_1_pin14),
    .pin15(n7486_1_pin7), .pin14(S0), .pin13(n7486_2_pin6), .pin12(n74153_1_pin12), .pin11(n74153_1_pin11),
    .pin10(n74283_1_pin1), .pin9(n74153_1_pin9));
  _7408 #(.ShowInternalStructure("true"), .VccGndPorts("true")) u_7408_1 (
    .pin1(A0), .pin2(B0), .pin3(n74153_1_pin5), .pin4(A1), .pin5(B1), .pin6(n74153_1_pin11),
    .pin7(n7486_1_pin7), .pin14(n7486_1_pin14), .pin13(B3), .pin12(A3), .pin11(n7408_1_pin11), .pin10(A2),
    .pin9(B2), .pin8(n7408_1_pin8));
  _74153 #(.ShowInternalStructure("true"), .VccGndPorts("true")) u_74153_2 (
    .pin1(n7486_1_pin7), .pin2(S1), .pin3(n7486_2_pin8), .pin4(n74153_2_pin4), .pin5(n7408_1_pin8),
    .pin6(n74283_1_pin13), .pin7(n74153_2_pin7), .pin8(n7486_1_pin7), .pin16(n7486_1_pin14),
    .pin15(n7486_1_pin7), .pin14(S0), .pin13(n7486_2_pin11), .pin12(n74153_2_pin12), .pin11(n7408_1_pin11),
    .pin10(n74283_1_pin10), .pin9(n74153_2_pin9));
  _7432 #(.ShowInternalStructure("true"), .VccGndPorts("true")) u_7432_1 (
    .pin1(A0), .pin2(B0), .pin3(n74153_1_pin4), .pin4(A1), .pin5(B1), .pin6(n74153_1_pin12),
    .pin7(n7486_1_pin7), .pin14(n7486_1_pin14), .pin13(A3), .pin12(B3), .pin11(n74153_2_pin12), .pin10(A2),
    .pin9(B2), .pin8(n74153_2_pin4));
  LED O0 (.in(n74153_1_pin7));
  LED O1 (.in(n74153_1_pin9));
  LED O2 (.in(n74153_2_pin7));
  LED O3 (.in(n74153_2_pin9));
  // also tied to GND on the sheet: n7486_1_pin7
  // also tied to VCC on the sheet: n7486_1_pin14

  // Notes on the sheet:
  //   Add: S1 = 0, S0 = 0, AS = 0
  //   Sub: S1 = 0, S0 = 0, AS = 1
  //   AND: S1 = 0, S0 = 1, AS = X
  //   OR: S1 = 1, S0 = 0, AS = X
  //   XOR: S1 = 1, S0 = 1, AS =X
  //   LSB
  //   MSB
endmodule

module AdderSub (
  input  Sub,
  input  B3,
  input  B2,
  input  B1,
  input  B0,
  input  A3,
  input  A2,
  input  A1,
  input  A0
);

  wire n7486_1_pin3, n7486_1_pin6, n7486_1_pin7, n7486_1_pin8, n7486_1_pin11, n7486_1_pin14, n74283_1_pin1,
       n74283_1_pin4, n74283_1_pin10, n74283_1_pin13;

  _7486 #(.ShowInternalStructure("true"), .VccGndPorts("true")) u_7486_1 (
    .pin1(B3), .pin2(Sub), .pin3(n7486_1_pin3), .pin4(B2), .pin5(Sub), .pin6(n7486_1_pin6),
    .pin7(n7486_1_pin7), .pin14(n7486_1_pin14), .pin13(B1), .pin12(Sub), .pin11(n7486_1_pin11), .pin10(B0),
    .pin9(Sub), .pin8(n7486_1_pin8));
  _74283 #(.ShowInternalStructure("true"), .VccGndPorts("true")) u_74283_1 (
    .pin1(n74283_1_pin1), .pin2(n7486_1_pin11), .pin3(A1), .pin4(n74283_1_pin4), .pin5(A0),
    .pin6(n7486_1_pin8), .pin7(Sub), .pin8(n7486_1_pin7), .pin16(n7486_1_pin14), .pin15(n7486_1_pin6),
    .pin14(A2), .pin13(n74283_1_pin13), .pin12(A3), .pin11(n7486_1_pin3), .pin10(n74283_1_pin10));  // open: pin9
  LED O3 (.in(n74283_1_pin10));
  LED O2 (.in(n74283_1_pin13));
  LED O1 (.in(n74283_1_pin1));
  LED O0 (.in(n74283_1_pin4));
  // also tied to GND on the sheet: n7486_1_pin7
  // also tied to VCC on the sheet: n7486_1_pin14

  // Notes on the sheet:
  //   bulasl
  //   B3
  //   B2
  //   B1
  //   B0
endmodule
